// Logisim project a.circ as structural Verilog: 5 circuits, main circuit main
// aoeu
module main (
  output [1:0] test
);


  assign test = 2'b11;
endmodule

module comb (
  input  A,
  input  B,
  input  C,
  output out_4
);

  wire and_1_out, not_1_out;

  or or_1 (out_4, and_1_out, not_1_out);
  and and_1 (and_1_out, B, A);
  not not_1 (not_1_out, C);
endmodule

module gates (
  input  _0_A,
  input  _0_B,
  input  _0_C,
  input  _1_A,
  input  _1_B,
  input  _1_C,
  input  _2_A,
  input  _2_B,
  input  _2_C,
  input  _3_A,
  input  _3_B,
  input  _3_C,
  input  _4_A,
  input  _4_B,
  input  _4_C,
  input  _5_A,
  input  _5_B,
  input  _5_C,
  input  _6,
  input  _7_A,
  input  _7_B,
  output _0,
  output _1,
  output _2,
  output _3,
  output _4,
  output _5,
  output _6_A,
  output _6_B,
  output _7_A_2,
  output _7_B_2
);

  and and_1 (_0, _0_A, ~_0_B, _0_C);  // AND_Gate
  nand nand_1 (_1, _1_A, ~_1_B, _1_C);  // NAND_Gate
  or or_1 (_2, _2_A, ~_2_B, _2_C);  // OR_Gate
  nor nor_1 (_3, _3_A, ~_3_B, _3_C);  // NOR_Gate
  ExactlyOne xor_1 (.out(_4), .in0(_4_A), .in2(_4_B), .in4(_4_C));
  NotExactlyOne xnor_1 (.out(_5), .in0(_5_A), .in2(_5_B), .in4(_5_C));
  buf buffer_1 (_6_A, _6);
  not not_1 (_6_B, _6);
  assign _7_A_2 = _7_B ? _7_A : 1'bz;  // Controlled_Buffer controlled_buffer_1
  assign _7_B_2 = _7_B ? ~_7_A : 1'bz;  // Controlled_Inverter controlled_inverter_1
endmodule

module wiring (
  input  [1:0] Input,
  input  Tunnel_In,
  output A,
  output B,
  output Tunnel_Out_A,
  output Tunnel_Out_B
);


  assign A = Input[0];
  assign B = Input[1];
  assign Tunnel_Out_A = Tunnel_In;
  assign Tunnel_Out_B = Tunnel_In;

  // Other names for the same wires on the sheet: A_t = Tunnel_In
endmodule

module memory (
  input  Register_In,
  input  Register_Load,
  input  Register_Clock,
  input  Register_Clear,
  output Register_Out
);

  Register register_1 ();  // open: D, en, Q, clk, clr
  Register #(.width(1)) register_2 (
    .D(Register_In), .en(Register_Load), .Q(Register_Out), .clk(Register_Clock), .clr(Register_Clear));
endmodule
