// Logisim project memory.circ as structural Verilog: 2 circuits, main circuit register
module register (
  input  Edge_Clock,
  input  Edge_In,
  input  Edge_Load,
  input  Edge_Clear,
  input  Level_Clock,
  input  Level_In,
  input  Level_Load,
  input  Level_Clear,
  input  in_9,
  input  in_10,
  input  [3:0] in_11,
  input  in_12,
  input  in_13,
  output R_Edge_Out,
  output F_Edge_Out,
  output H_Level_Out,
  output L_Level_Out
);

  wire [3:0] counter_1_q;

  Register #(.width(1)) register_1 (.D(Edge_In), .en(Edge_Load), .Q(R_Edge_Out), .clk(Edge_Clock), .clr(Edge_Clear));
  Register #(.width(1), .trigger("falling")) register_2 (
    .D(Edge_In), .en(Edge_Load), .Q(F_Edge_Out), .clk(Edge_Clock), .clr(Edge_Clear));
  Register #(.width(1), .trigger("high")) register_3 (
    .D(Level_In), .en(Level_Load), .Q(H_Level_Out), .clk(Level_Clock), .clr(Level_Clear));
  Register #(.width(1), .trigger("low")) register_4 (
    .D(Level_In), .en(Level_Load), .Q(L_Level_Out), .clk(Level_Clock), .clr(Level_Clear));
  Register register_5 ();  // open: D, en, Q, clk, clr
  Counter #(.width(4), .max('hf)) counter_1 (
    .load(in_10), .D(in_11), .count(in_12), .Q(counter_1_q), .clk(in_13));  // open: carry, clr
  // Probe on counter_1_q
  D_Flip_Flop d_ff_1 ();  // open: clk, D, Q, Qn, preset, en, reset
  Counter counter_2 ();  // open: load, D, count, Q, carry, clk, clr
  J_K_Flip_Flop j_k_ff_1 (.preset(in_9), .reset(in_9));  // open: J, clk, K, Q, Qn, en
  ROM rom_1 ();  // open: addr, data, sel
  RAM ram_1 ();  // open: addr, data, sel, clk, ld, clr
endmodule

module flip_flops (
  input  DT_FlipFlop_Clock,
  input  DT_FlipFlop_Data,
  input  DT_FlipFlop_Load,
  output D_Q1,
  output D_Q0,
  output T_Q1,
  output T_Q0
);

  D_Flip_Flop d_ff_1 (
    .clk(DT_FlipFlop_Clock), .D(DT_FlipFlop_Data), .Q(D_Q1), .Qn(D_Q0), .en(DT_FlipFlop_Load));  // open: preset, reset
  T_Flip_Flop t_ff_1 (
    .clk(DT_FlipFlop_Clock), .T(DT_FlipFlop_Data), .Q(T_Q1), .Qn(T_Q0), .en(DT_FlipFlop_Load));  // open: preset, reset
endmodule
