// Logisim project wiring.circ as structural Verilog: 3 circuits, main circuit wiring
module wiring (
  input  in_1,
  input  _0,
  input  _1,
  input  _2,
  input  _3,
  input  _3_2,
  output out_7,
  output _0_2,
  output _1_2,
  output _2_2,
  output _3_3,
  output [1:0] _4
);


  assign _0_2 = _0;
  assign _1_2 = _1;
  assign _2_2 = _2;
  assign _3_2 = _3;
  assign _3_3 = _3;
  assign _4 = 2'b11;
endmodule

module splitters (
  input  [1:0] LH_2,
  input  [1:0] LH_1,
  input  [1:0] LH_0,
  input  [1:0] LH_3,
  input  [1:0] RH_0,
  input  [1:0] RH_1,
  input  [1:0] RH_2,
  input  [1:0] RH_3,
  input  [1:0] C_1,
  input  [1:0] C_0,
  input  [1:0] C_2,
  input  [1:0] C_3,
  input  [1:0] L_1,
  input  [1:0] L_0,
  input  [1:0] L_2,
  input  [1:0] L_3,
  input  [2:0] FAN_3,
  input  [2:0] FAN_2,
  output LH_0_A,
  output LH_2_A,
  output LH_3_B,
  output LH_3_A,
  output LH_0_B,
  output LH_2_B,
  output LH_1_B,
  output LH_1_A,
  output RH_0_A,
  output RH_2_A,
  output RH_3_B,
  output RH_3_A,
  output RH_0_B,
  output RH_2_B,
  output RH_1_B,
  output RH_1_A,
  output C_0_A,
  output C_2_A,
  output C_3_B,
  output C_3_A,
  output C_0_B,
  output C_2_B,
  output C_1_B,
  output C_1_A,
  output L_0_A,
  output L_2_A,
  output L_3_B,
  output L_3_A,
  output L_0_B,
  output L_2_B,
  output L_1_B,
  output L_1_A,
  output [1:0] FAN_2_2,
  output out_52,
  output [1:0] FAN_3_2
);


  assign C_0_A = C_0[0];
  assign C_0_B = C_0[1];
  assign C_1_A = C_1[0];
  assign C_1_B = C_1[1];
  assign C_2_A = C_2[0];
  assign C_2_B = C_2[1];
  assign C_3_A = C_3[0];
  assign C_3_B = C_3[1];
  assign FAN_2_2 = FAN_2[1:0];
  assign FAN_3_2 = {FAN_3[0], FAN_3[1]};
  assign L_0_A = L_0[0];
  assign L_0_B = L_0[1];
  assign L_1_A = L_1[0];
  assign L_1_B = L_1[1];
  assign L_2_A = L_2[0];
  assign L_2_B = L_2[1];
  assign L_3_A = L_3[0];
  assign L_3_B = L_3[1];
  assign LH_0_A = LH_0[0];
  assign LH_0_B = LH_0[1];
  assign LH_1_A = LH_1[0];
  assign LH_1_B = LH_1[1];
  assign LH_2_A = LH_2[0];
  assign LH_2_B = LH_2[1];
  assign LH_3_A = LH_3[0];
  assign LH_3_B = LH_3[1];
  assign RH_0_A = RH_0[0];
  assign RH_0_B = RH_0[1];
  assign RH_1_A = RH_1[0];
  assign RH_1_B = RH_1[1];
  assign RH_2_A = RH_2[0];
  assign RH_2_B = RH_2[1];
  assign RH_3_A = RH_3[0];
  assign RH_3_B = RH_3[1];
endmodule

module tunnels (
  input  _0,
  input  _1,
  input  _1_2,
  output _0_2,
  output _1_3,
  output _1_4
);


  assign _0_2 = _0;
  assign _1_2 = _1;
  assign _1_3 = _1;
  assign _1_4 = _1;
endmodule
